// Digital circuit ASM4bit.dig as structural Verilog
module ASM4bit (
  input  [3:0] A,
  input  [3:0] B,
  input  [1:0] F,
  output out_4,
  output out_5,
  output out_6,
  output out_7,
  output out_8,
  output out_9,
  output out_10,
  output out_11
);

  ASM4 #(.applicationType("GHDL")) u_ASM4 (
    .A(A), .B(B), .F(F), .S({out_11, out_10, out_9, out_8, out_7, out_6, out_5, out_4}));
endmodule

/* Code of ASM4:
-- ASM4 stands for Adder-Subtracter-Multiplyer 4 bits

LIBRARY ieee;
USE ieee.std_logic_1164.all;
USE ieee.numeric_std.all;

entity ASM4 is
    port(
        A, B: in std_logic_vector(3 downto 0);
        F: in std_logic_vector(1 downto 0); -- Function selecting
        S: out std_logic_vector(7 downto 0)
    );
end ASM4;

architecture Equations of ASM4 is
    signal results: integer := 0;
    begin
        with F select
        results <= 
            to_integer(unsigned(A)) + to_integer(unsigned(B)) when "00",
            to_integer(unsigned(A)) - to_integer(unsigned(B)) when "01",
            to_integer(unsigned(A)) * to_integer(unsigned(B)) when "10",
            0 when others;
        S <= std_logic_vector(to_unsigned(results, 8));
end Equations;
*/
