// Digital circuit hw_2_decoder.dig as structural Verilog
module hw_2_decoder (
  input  x3,
  input  x2,
  input  x1,
  input  x0,
  input  y3,
  input  y2,
  input  y1,
  input  y0,
  input  c01,
  input  c00,
  output c41,
  output c40
);

  hw_2_decoder_1_bit_comparator hw_2_decoder_1_bit_comparator_1 ();  // open: input, c_i_plus_1_0, c_i_plus_1_1
  hw_2_decoder_1_bit_comparator hw_2_decoder_1_bit_comparator_2 ();  // open: input, c_i_plus_1_0, c_i_plus_1_1
  hw_2_decoder_1_bit_comparator hw_2_decoder_1_bit_comparator_3 ();  // open: input, c_i_plus_1_0, c_i_plus_1_1
  hw_2_decoder_1_bit_comparator hw_2_decoder_1_bit_comparator_4 ();  // open: input, c_i_plus_1_0, c_i_plus_1_1
endmodule
