// Digital circuit q22_abff.dig as structural Verilog
module q22_abff (
  input  clk,
  input  A,
  input  B,
  output Q1_plus
);

  wire and_1_out, and_2_out, not_1_out, srff_1_q_2;

  not not_1 (not_1_out, B);
  and and_1 (and_1_out, srff_1_q_2, A);
  and and_2 (and_2_out, not_1_out, Q1_plus);
  SRFF srff_1 (.S(and_1_out), .R(and_2_out), .CLK(clk), .Q(Q1_plus), .Q_2(srff_1_q_2));

  // Notes on the sheet:
  //   SR -> JK -> AB
endmodule
